# Fritzing sketch Schematic (saved by Fritzing 0.9.3b)

parts:
  Raspberry_Pi_1 = Raspberry Pi 3 [part_number=RPI-3-V1.2]
  KY-1 = Keyes Relay [package=THT]
  KY-2 = Keyes Relay [package=THT]
  KY-3 = Keyes Relay [package=THT]
  M1 = RioRand LM2596
  F1 = Fan - Ventilador [package=THT]
  F2 = Fan - Ventilador [package=THT]
  J1 = XT60 Connector [package=THT]
  J2 = XT60 Connector [package=THT]
  J3 = XT60 Connector [package=THT]

nets:
  N1: Raspberry_Pi_1.GIPO4, KY-2.signal
  N2: Raspberry_Pi_1.GIPO18, KY-1.signal, KY-3.signal
  GND: Raspberry_Pi_1.GND, KY-1.ground, KY-2.ground, KY-3.ground, M1.Pin_4, F1.GND, F2.GND
  5V: Raspberry_Pi_1.5V, KY-1.power, KY-2.power, KY-3.power, M1.Pin_3, F1.5V
  N3: KY-1.NC, KY-1.NO, J2.VCC
  VCC: KY-1.C, M1.Pin_2, J1.VCC, J3.VCC
  N4: KY-2.NC, KY-2.NO, J3.GND
  N5: KY-2.C, KY-3.C, M1.Pin_1, J1.GND
  N6: KY-3.NC, KY-3.NO, J2.GND

notes:
  female
  male
  DC 24V IN
  24V Led OUT
  24V Printer OUT
  5V OUT
  5V Fan

custom parts:
  Keyes Relay: The Keyes 5V relay module is suitable for SCM development, home appliance control. It uses a 5V~12V TIL control signal which can control DC / AC signal.
  Fan - Ventilador: Ventilador de 2 pines, se encuentra comunmente en computadoras de escritorio
  XT60 Connector: Yellow XT60 connector for high current loads up to 40A
